# Fritzing sketch Nerdy Derby (saved by Fritzing 0.9.3b)

parts:
  Componente1 = Arduino Uno (Rev3)
  M1 = RioRand LM2596
  Power_plug1 = Power plug
  J1 = Basic Servo
  J2 = Basic Servo
  J3 = Basic Servo
  R3 = Resistor [tolerance=±5% resistance=220 package="1206 [SMD]"]
  R2 = Resistor [tolerance=±5% resistance=220 package="1206 [SMD]"]
  R1 = Resistor [tolerance=±5% resistance=220 package="1206 [SMD]"]
  LED3 = LEDs [package=led10mm]
  LED2 = LEDs [package=led10mm]
  LED1 = LEDs [package=led10mm]
  LED4 = LED - 5mm [color="Infrared (940nm)" package="5 mm [THT]"]
  LED5 = LED - 5mm [color="Infrared (940nm)" package="5 mm [THT]"]
  LED6 = LED - 5mm [color="Infrared (940nm)" package="5 mm [THT]"]
  R4 = Resistor [tolerance=±5% resistance=10k package=THT]
  R5 = Resistor [tolerance=±5% resistance=10k package=THT]
  R6 = Resistor [tolerance=±5% resistance=10k package=THT]

nets:
  N1: Componente1.A0, LED6.cathode, R6.Pin_0
  N2: Componente1.A1, LED5.cathode, R5.Pin_0
  N3: Componente1.A2, LED4.cathode, R4.Pin_0
  N4: Componente1.D8, J1.pulse, J2.pulse, J3.pulse
  VCC: Componente1.5V, M1.Out+, J1.vcc, J2.vcc, J3.vcc, LED4.anode, LED5.anode, LED6.anode
  N5: Componente1.GND, M1.Out-, LED3.C, LED2.C, LED1.C, R4.Pin_1, R5.Pin_1, R6.Pin_1
  N6: M1.In+, Power_plug1.VCC, R3.Pin_0, R2.Pin_0, R1.Pin_0
  GND: M1.In-, Power_plug1.GND, J1.gnd, J2.gnd, J3.gnd
  N7: R3.Pin_1, LED1.A
  N8: R2.Pin_1, LED2.A
  N9: R1.Pin_1, LED3.A

notes:
  Sensores e Servos

custom parts:
  RioRand LM2596: Step-down DC-DC Converter (modified to correct all views by Peter Van Epp january 2018) Corrected the pins so the part works in all views. Changed the sizes in bb and pcb to match the data sheet. PCB view had a small outline (possibly only for wires), changed it to pads in the same places as the module and added holes in the PCB silkscreen layer where the mounting holes on the module are (you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
